// Logisim project Adder-Sub.circ as structural Verilog: 5 circuits, main circuit main
module main (
  input  [2:0] A,
  input  [2:0] B,
  input  Operation,
  output X0,
  output X1,
  output X2,
  output sign
);

  wire comp2_1_x0, comp2_1_x1, comp2_1_x2, comp2_1_x3, comp2_2_x0, comp2_2_x1, comp2_2_x2, comp2_2_x3,
       total_fa_1_x0, total_fa_1_x1, total_fa_1_x2, xor_1_out;

  xor xor_1 (xor_1_out, B[2], Operation);
  comp2 comp2_1 (
    .Sign(A[2]), .A2(1'b0), .A1(A[1]), .A0(A[0]), .X0(comp2_1_x0), .X1(comp2_1_x1), .X2(comp2_1_x2),
    .x3(comp2_1_x3));
  comp2 comp2_2 (
    .Sign(xor_1_out), .A2(1'b0), .A1(B[1]), .A0(B[0]), .X0(comp2_2_x0), .X1(comp2_2_x1), .X2(comp2_2_x2),
    .x3(comp2_2_x3));
  Total_FA total_fa_1 (
    .Ao(comp2_1_x0), .A1(comp2_1_x1), .A2(comp2_1_x2), .A3(comp2_1_x3), .Bo(comp2_2_x0), .B1(comp2_2_x1),
    .B2(comp2_2_x2), .B3(comp2_2_x3), .x0(total_fa_1_x0), .x1(total_fa_1_x1), .x2(total_fa_1_x2), .x3(sign));  // open: Carry
  comp2 comp2_3 (
    .Sign(sign), .A2(total_fa_1_x2), .A1(total_fa_1_x1), .A0(total_fa_1_x0), .X0(X0), .X1(X1), .X2(X2));  // open: x3
endmodule

module FA (
  input  Ao,
  input  Bo,
  input  The_Carry,
  output Carry,
  output Sum
);

  wire ha_1_carry, ha_1_sum, ha_2_carry;

  HA ha_1 (.in_1(Ao), .in_2(Bo), .Sum(ha_1_sum), .Carry(ha_1_carry));
  HA ha_2 (.in_1(ha_1_sum), .in_2(The_Carry), .Sum(Sum), .Carry(ha_2_carry));
  or or_1 (Carry, ha_1_carry, ha_2_carry);
endmodule

module Total_FA (
  input  Ao,
  input  A1,
  input  A2,
  input  A3,
  input  Bo,
  input  B1,
  input  B2,
  input  B3,
  output x0,
  output x1,
  output x2,
  output x3,
  output Carry
);

  wire fa_1_carry, fa_2_carry, ha_1_carry;

  HA ha_1 (.in_1(Ao), .in_2(Bo), .Sum(x0), .Carry(ha_1_carry));
  FA fa_1 (.Ao(A1), .Bo(B1), .The_Carry(ha_1_carry), .Carry(fa_1_carry), .Sum(x1));
  FA fa_2 (.Ao(A2), .Bo(B2), .The_Carry(fa_1_carry), .Carry(fa_2_carry), .Sum(x2));
  FA fa_3 (.Ao(A3), .Bo(B3), .The_Carry(fa_2_carry), .Carry(Carry), .Sum(x3));
endmodule

module HA (
  input  in_1,
  input  in_2,
  output Sum,
  output Carry
);

  xor xor_1 (Sum, in_1, in_2);
  and and_1 (Carry, in_1, in_2);
endmodule

module comp2 (
  input  Sign,
  input  A2,
  input  A1,
  input  A0,
  output X0,
  output X1,
  output X2,
  output x3
);

  wire xor_1_out, xor_2_out, xor_3_out;

  xor xor_1 (xor_1_out, Sign, A2);
  xor xor_2 (xor_2_out, Sign, A1);
  xor xor_3 (xor_3_out, A0, Sign);
  Total_FA total_fa_1 (
    .Ao(Sign), .A1(1'b0), .A2(1'b0), .A3(1'b0), .Bo(xor_3_out), .B1(xor_2_out), .B2(xor_1_out), .B3(Sign),
    .x0(X0), .x1(X1), .x2(X2), .x3(x3));  // open: Carry
endmodule
