// Logisim project Final circuit.circ as structural Verilog: 2 circuits, main circuit main
module main (
  input  [2:0] input_1,
  input  [2:0] input_2,
  input  [1:0] Operation
);

  wire alu_1_c0, alu_1_c1, alu_1_c2, alu_1_c3, alu_1_div_by_zero_flag, alu_1_sign, alu_1_zero_output_flag,
       n7448_1_p10, n7448_1_p11, n7448_1_p12, n7448_1_p13, n7448_1_p14, n7448_1_p15, n7448_1_p16;

  ALU alu_1 (
    .input_1(input_1), .input_2(input_2), .Operation(Operation), .Sign(alu_1_sign),
    .div_by_zero_Flag(alu_1_div_by_zero_flag), .C0(alu_1_c0), .Zero_output_Flag(alu_1_zero_output_flag),
    .C1(alu_1_c1), .C2(alu_1_c2), .C3(alu_1_c3));
  // _7448 7448_1: pin names not known; wires that end beside it: alu_1_c1, alu_1_c2, 1'b1, 1'b0, 1'b1, alu_1_c3, alu_1_c0, 1'b0, 1'b1, n7448_1_p10, n7448_1_p11, n7448_1_p12, n7448_1_p13, n7448_1_p14, n7448_1_p15, n7448_1_p16
  _7_Segment_Display u_7_segment_display_1 (
    .g(alu_1_sign), .f(1'b0), .a(1'b0), .b(1'b0), .e(1'b0), .d(1'b0), .c(1'b0), .dp(1'b0));
  _7_Segment_Display u_7_segment_display_2 (
    .g(n7448_1_p11), .f(n7448_1_p10), .a(n7448_1_p12), .b(n7448_1_p13), .e(n7448_1_p16), .d(n7448_1_p15),
    .c(n7448_1_p14), .dp(1'b0));
  LED Sign (.in(alu_1_sign));
  LED Zero_Output (.in(alu_1_zero_output_flag));
  LED Div_by_zero (.in(alu_1_div_by_zero_flag));

  // Notes on the sheet:
  //   00->Multiplication
  //   01 ->Addition
  //   10 ->Remainder
  //   11 -> Subtraction
endmodule

module ALU (
  input  [2:0] input_1,
  input  [2:0] input_2,
  input  [1:0] Operation,
  output C0,
  output C1,
  output Zero_output_Flag,
  output div_by_zero_Flag,
  output C2,
  output C3,
  output Sign
);

  wire Adder_Sub_sign, Adder_Sub_x0, Adder_Sub_x1, Adder_Sub_x2, multiplexer_5_out, Multiplier_c0,
       Multiplier_c1, Multiplier_c2, Multiplier_c3, Multiplier_sign, not_1_out, Remainder_flag, Remainder_r0,
       Remainder_r1, Remainder_rs;

  multiplier_final_main Multiplier (
    .input_1(input_1), .input_2(input_2), .sign(Multiplier_sign), .c0(Multiplier_c0), .c1(Multiplier_c1),
    .c2(Multiplier_c2), .c3(Multiplier_c3));
  Adder_Sub_main Adder_Sub (
    .A(input_1), .B(input_2), .Operation(Operation[1]), .X0(Adder_Sub_x0), .X1(Adder_Sub_x1),
    .X2(Adder_Sub_x2), .sign(Adder_Sub_sign));
  Remainder Remainder (
    .A(input_1), .B(input_2), .RS(Remainder_rs), .R1(Remainder_r1), .R0(Remainder_r0), .Flag(Remainder_flag));
  Multiplexer #(.select(2)) multiplexer_1 (
    .in0(Multiplier_c0), .in1(Adder_Sub_x0), .in2(Remainder_r0), .in3(Adder_Sub_x0), .out(C0),
    .sel(Operation), .en(1'b1));
  Multiplexer #(.select(2)) multiplexer_2 (
    .in0(Multiplier_c1), .in1(Adder_Sub_x1), .in2(Remainder_r1), .in3(Adder_Sub_x1), .out(C1),
    .sel(Operation), .en(1'b1));
  Multiplexer #(.select(2)) multiplexer_3 (
    .in0(Multiplier_c2), .in1(Adder_Sub_x2), .in2(1'b0), .in3(Adder_Sub_x2), .out(C2), .sel(Operation),
    .en(1'b1));
  Multiplexer #(.select(2)) multiplexer_4 (
    .in0(Multiplier_c3), .in1(1'b0), .in2(1'b0), .in3(1'b0), .out(C3), .sel(Operation), .en(1'b1));
  Multiplexer #(.select(2)) multiplexer_5 (
    .in0(Multiplier_sign), .in1(Adder_Sub_sign), .in2(Remainder_rs), .in3(Adder_Sub_sign),
    .out(multiplexer_5_out), .sel(Operation), .en(1'b1));
  Multiplexer #(.select(2)) multiplexer_6 (
    .in0(1'b0), .in1(1'b0), .in2(Remainder_flag), .in3(1'b0), .out(div_by_zero_Flag), .sel(Operation),
    .en(1'b1));
  nor nor_1 (Zero_output_Flag, C0, C1, C2, C3);
  not not_1 (not_1_out, Zero_output_Flag);
  and and_1 (Sign, not_1_out, multiplexer_5_out);

  // Notes on the sheet:
  //   Bit 1
  //   Bit2
  //   Bit 3
  //   Bit 4
  //   Sign & Flag
endmodule
