// Logisim project Remainder Circuit.circ as structural Verilog: 1 circuit, main circuit Remainder
module Remainder (
  input  [2:0] A,
  input  [2:0] B,
  output RS,
  output R1,
  output R0,
  output Flag
);

  wire and_1_out, and_2_out, and_3_out, and_4_out, not_1_out, not_2_out, not_3_out, not_4_out;

  not not_1 (not_1_out, A[0]);
  not not_2 (not_2_out, B[0]);
  not not_3 (not_3_out, B[1]);
  and and_1 (and_1_out, A[1], not_1_out);
  and and_2 (and_2_out, B[1], B[0]);
  and and_3 (and_3_out, A[1], B[0]);
  and and_4 (and_4_out, A[0], B[1]);
  and and_5 (Flag, not_2_out, not_3_out);
  and and_6 (R1, and_1_out, and_2_out);
  not not_4 (not_4_out, and_3_out);
  and and_7 (R0, not_4_out, and_4_out);

  assign RS = A[2];
endmodule
