// Logisim project multiplier final.circ as structural Verilog: 2 circuits, main circuit main
module main (
  input  [2:0] input_1,
  input  [2:0] input_2,
  output sign,
  output c0,
  output c1,
  output c2,
  output c3
);

  wire and_2_out, and_3_out, and_4_out, ha_1_carry;

  xor xor_1 (sign, input_1[2], input_2[2]);
  and and_1 (c0, input_1[0], input_2[0]);
  and and_2 (and_2_out, input_1[1], input_2[0]);
  and and_3 (and_3_out, input_1[0], input_2[1]);
  and and_4 (and_4_out, input_1[1], input_2[1]);
  HA ha_1 (.in_1(and_2_out), .in_2(and_3_out), .sum(c1), .carry(ha_1_carry));
  HA ha_2 (.in_1(ha_1_carry), .in_2(and_4_out), .sum(c2), .carry(c3));

  // Notes on the sheet:
  //   ALL And gates--> IC 1
  //   Gate 4
  //   Gate 3
  //   Gate 2
  //   Gate 1
  //   A0B0
  //   A1B0
  //   A0B1
  //   A1B1
  //   P0
  //   P1
  //   P2
  //   P3
  //   And of half adders-->IC2
endmodule

module HA (
  input  in_1,
  input  in_2,
  output sum,
  output carry
);

  xor xor_1 (sum, in_1, in_2);
  and and_1 (carry, in_2, in_1);
endmodule
